// Logisim project Lab5.circ as structural Verilog: 11 circuits, main circuit main
module main (
  input  [31:0] in_1
);

  wire alu_control_1_alu_src, and_1_out, clock_1_out, comparator_1_eq, control_1_branch, control_1_memread,
       control_1_memtoreg, control_1_memwrite, control_1_regwrite;
  wire [3:0] alu_control_1_alu_ctrl0;
  wire [4:0] undriven;
  wire [7:0] register_1_q_2;
  wire [23:0] register_1_q;
  wire [31:0] adder_1_out, adder_2_out, datamemory_1_readdata, fullalu_1_s, immgen_1_imm32,
       instructionmemory_1_instructions, multiplexer_1_out, multiplexer_2_out, multiplexer_3_out,
       regi_1_rdata1, regi_1_rdata2;

  Register #(.width(32)) register_1 (
    .D(multiplexer_2_out), .en(1'b1), .clk(clock_1_out), .Q({register_1_q_2, register_1_q}));  // open: clr
  Clock clock_1 (.out(clock_1_out));
  Adder #(.width(32)) adder_1 (.a({register_1_q_2, register_1_q}), .b(in_1), .out(adder_1_out));  // open: cin, cout
  InstructionMemory instructionmemory_1 (
    .Address(register_1_q), .Clock_in(clock_1_out), .Instructions(instructionmemory_1_instructions));
  Control control_1 (
    .I6(instructionmemory_1_instructions[6]), .I5(instructionmemory_1_instructions[5]),
    .I4(instructionmemory_1_instructions[4]), .I3(instructionmemory_1_instructions[3]),
    .I2(instructionmemory_1_instructions[2]), .I1(instructionmemory_1_instructions[1]),
    .I0(instructionmemory_1_instructions[0]), .MemtoReg(control_1_memtoreg), .RegWrite(control_1_regwrite),
    .MemRead(control_1_memread), .MemWrite(control_1_memwrite), .Branch(control_1_branch));
  regi regi_1 (
    .RReg1(instructionmemory_1_instructions[19:15]), .RReg2(undriven), .WData(multiplexer_3_out),
    .Clock_in(clock_1_out), .Write(control_1_regwrite), .WReg(instructionmemory_1_instructions[11:7]),
    .RData1(regi_1_rdata1), .RData2(regi_1_rdata2));
  ImmGen immgen_1 (.Instructions(instructionmemory_1_instructions), .IMM32(immgen_1_imm32));
  ALU_control alu_control_1 (
    .I30(instructionmemory_1_instructions[30]), .I14(instructionmemory_1_instructions[14]),
    .I13(instructionmemory_1_instructions[13]), .I12(instructionmemory_1_instructions[12]),
    .I6(instructionmemory_1_instructions[6]), .I5(instructionmemory_1_instructions[5]),
    .I4(instructionmemory_1_instructions[4]), .ALU_CTRL3(alu_control_1_alu_ctrl0[3]),
    .ALU_CTRL2(alu_control_1_alu_ctrl0[2]), .ALU_CTRL1(alu_control_1_alu_ctrl0[1]),
    .ALU_CTRL0(alu_control_1_alu_ctrl0[0]), .ALU_SRC(alu_control_1_alu_src));
  Multiplexer #(.enable("false"), .width(32)) multiplexer_1 (
    .in0(regi_1_rdata2), .in1(immgen_1_imm32), .out(multiplexer_1_out), .sel(alu_control_1_alu_src));
  Comparator #(.width(32)) comparator_1 (.a(regi_1_rdata1), .b(regi_1_rdata2), .eq(comparator_1_eq));  // open: gt, lt
  Adder #(.width(32)) adder_2 (
    .a({register_1_q_2, register_1_q}), .b(immgen_1_imm32), .out(adder_2_out));  // open: cin, cout
  fullALU fullalu_1 (
    .in_1(alu_control_1_alu_ctrl0), .A(regi_1_rdata1), .B(multiplexer_1_out), .S(fullalu_1_s));  // open: C_out
  Multiplexer #(.enable("false"), .width(32)) multiplexer_2 (
    .in0(adder_1_out), .in1(adder_2_out), .out(multiplexer_2_out), .sel(and_1_out));
  and and_1 (and_1_out, control_1_branch, comparator_1_eq);
  DataMemory datamemory_1 (
    .Address(fullalu_1_s[25:0]), .MemWrite(control_1_memwrite), .MemRead(control_1_memread),
    .Clock_In(clock_1_out), .WriteData(regi_1_rdata2), .ReadData(datamemory_1_readdata));
  Multiplexer #(.enable("false"), .width(32)) multiplexer_3 (
    .in0(fullalu_1_s), .in1(datamemory_1_readdata), .out(multiplexer_3_out), .sel(control_1_memtoreg));
endmodule

module adder (
  input  A,
  input  B,
  input  C_in,
  output S,
  output C_out
);

  wire and_1_out, and_2_out, and_3_out, and_4_out, and_5_out, and_6_out, and_7_out, not_1_out, not_2_out,
       not_3_out;

  not not_1 (not_1_out, A);
  not not_2 (not_2_out, B);
  not not_3 (not_3_out, C_in);
  and and_1 (and_1_out, not_1_out, not_2_out, C_in);
  and and_2 (and_2_out, not_1_out, B, not_3_out);
  and and_3 (and_3_out, A, not_2_out, not_3_out);
  and and_4 (and_4_out, A, B, C_in);
  and and_5 (and_5_out, B, C_in);
  and and_6 (and_6_out, A, C_in);
  and and_7 (and_7_out, A, B);
  or or_1 (S, and_1_out, and_2_out, and_3_out, and_4_out);
  or or_2 (C_out, and_5_out, and_6_out, and_7_out);
endmodule

module ALU (
  input  [3:0] in_1,
  input  A,
  input  B,
  input  C_in,
  output S,
  output C_out
);

  wire adder_1_s, and_1_out, multiplexer_1_out, not_1_out, or_1_out, xor_1_out;

  Multiplexer #(.enable("false")) multiplexer_1 (.in0(B), .in1(not_1_out), .out(multiplexer_1_out), .sel(in_1[2]));
  not not_1 (not_1_out, B);
  adder adder_1 (.A(A), .B(multiplexer_1_out), .C_in(C_in), .S(adder_1_s), .C_out(C_out));
  and and_1 (and_1_out, A, multiplexer_1_out);
  or or_1 (or_1_out, A, multiplexer_1_out);
  xor xor_1 (xor_1_out, A, multiplexer_1_out);
  Multiplexer #(.disabled("Z"), .enable("false"), .select(2)) multiplexer_2 (
    .in0(and_1_out), .in1(or_1_out), .in2(xor_1_out), .in3(adder_1_s), .out(S), .sel(in_1[1:0]));
endmodule

module fourALU (
  input  [3:0] in_1,
  input  [3:0] A,
  input  [3:0] B,
  input  C_in,
  output [3:0] out_5,
  output C_out
);

  wire alu_1_c_out, alu_2_c_out, alu_3_c_out;

  ALU alu_1 (.in_1(in_1), .A(A[0]), .B(B[0]), .C_in(C_in), .S(out_5[0]), .C_out(alu_1_c_out));
  ALU alu_2 (.in_1(in_1), .A(A[1]), .B(B[1]), .C_in(alu_1_c_out), .S(out_5[1]), .C_out(alu_2_c_out));
  ALU alu_3 (.in_1(in_1), .A(A[2]), .B(B[2]), .C_in(alu_2_c_out), .S(out_5[2]), .C_out(alu_3_c_out));
  ALU alu_4 (.in_1(in_1), .A(A[3]), .B(B[3]), .C_in(alu_3_c_out), .S(out_5[3]), .C_out(C_out));
endmodule

module fullALU (
  input  [3:0] in_1,
  input  [31:0] A,
  input  [31:0] B,
  output [31:0] S,
  output C_out
);

  wire fouralu_1_c_out, fouralu_2_c_out, fouralu_3_c_out, fouralu_4_c_out, fouralu_5_c_out, fouralu_6_c_out,
       fouralu_7_c_out;

  fourALU fouralu_1 (.in_1(in_1), .A(A[3:0]), .B(B[3:0]), .C_in(in_1[2]), .out_5(S[3:0]), .C_out(fouralu_1_c_out));
  fourALU fouralu_2 (
    .in_1(in_1), .A(A[7:4]), .B(B[7:4]), .C_in(fouralu_1_c_out), .out_5(S[7:4]), .C_out(fouralu_2_c_out));
  fourALU fouralu_3 (
    .in_1(in_1), .A(A[11:8]), .B(B[11:8]), .C_in(fouralu_2_c_out), .out_5(S[11:8]), .C_out(fouralu_3_c_out));
  fourALU fouralu_4 (
    .in_1(in_1), .A(A[15:12]), .B(B[15:12]), .C_in(fouralu_3_c_out), .out_5(S[15:12]), .C_out(fouralu_4_c_out));
  fourALU fouralu_5 (
    .in_1(in_1), .A(A[19:16]), .B(B[19:16]), .C_in(fouralu_4_c_out), .out_5(S[19:16]), .C_out(fouralu_5_c_out));
  fourALU fouralu_6 (
    .in_1(in_1), .A(A[23:20]), .B(B[23:20]), .C_in(fouralu_5_c_out), .out_5(S[23:20]), .C_out(fouralu_6_c_out));
  fourALU fouralu_7 (
    .in_1(in_1), .A(A[27:24]), .B(B[27:24]), .C_in(fouralu_6_c_out), .out_5(S[27:24]), .C_out(fouralu_7_c_out));
  fourALU fouralu_8 (.in_1(in_1), .A(A[31:28]), .B(B[31:28]), .C_in(fouralu_7_c_out), .out_5(S[31:28]), .C_out(C_out));
endmodule

module ALU_control (
  input  I30,
  input  I14,
  input  I13,
  input  I12,
  input  I6,
  input  I5,
  input  I4,
  output ALU_CTRL3,
  output ALU_CTRL2,
  output ALU_CTRL1,
  output ALU_CTRL0,
  output ALU_SRC
);

  wire and_3_out, and_4_out, and_5_out, and_6_out, and_7_out, not_1_out, not_2_out, not_3_out, not_4_out,
       not_5_out, not_6_out;

  not not_1 (not_1_out, I30);
  not not_2 (not_2_out, I14);
  not not_3 (not_3_out, I13);
  not not_4 (not_4_out, I12);
  not not_5 (not_5_out, I5);
  not not_6 (not_6_out, I4);
  and and_1 (ALU_CTRL3, not_3_out, I12);
  and and_2 (ALU_CTRL2, I30, not_3_out, not_4_out, I5);
  and and_3 (and_3_out, not_3_out, not_4_out);
  and and_4 (and_4_out, I30, not_3_out);
  and and_5 (and_5_out, not_2_out, not_4_out);
  and and_6 (and_6_out, I13, not_4_out);
  and and_7 (and_7_out, not_1_out, I14, not_3_out, I12);
  or or_1 (ALU_SRC, not_5_out, not_6_out);
  or or_2 (ALU_CTRL1, and_3_out, not_6_out, and_4_out);
  or or_3 (ALU_CTRL0, and_5_out, and_6_out, and_7_out);
endmodule

module regi (
  input  [4:0] RReg1,
  input  [4:0] RReg2,
  input  [31:0] WData,
  input  Clock_in,
  input  Write,
  input  [4:0] WReg,
  output [31:0] RData1,
  output [31:0] RData2
);

  wire demultiplexer_1_out0, demultiplexer_1_out1, demultiplexer_1_out2, demultiplexer_1_out3,
       demultiplexer_1_out4, demultiplexer_1_out5, demultiplexer_1_out6, demultiplexer_1_out7,
       demultiplexer_1_out8, demultiplexer_1_out9, demultiplexer_1_out10, demultiplexer_1_out11,
       demultiplexer_1_out12, demultiplexer_1_out13, demultiplexer_1_out14, demultiplexer_1_out15,
       demultiplexer_1_out16, demultiplexer_1_out17, demultiplexer_1_out18, demultiplexer_1_out19,
       demultiplexer_1_out20, demultiplexer_1_out21, demultiplexer_1_out22, demultiplexer_1_out23,
       demultiplexer_1_out24, demultiplexer_1_out25, demultiplexer_1_out26, demultiplexer_1_out27,
       demultiplexer_1_out28, demultiplexer_1_out29, demultiplexer_1_out30, demultiplexer_1_out31, undriven,
       undriven_2, undriven_3, undriven_4, undriven_5, undriven_6, undriven_7, undriven_8, undriven_9,
       undriven_10, undriven_11, undriven_12, undriven_13, undriven_14, undriven_15;
  wire [31:0] register_1_q, register_2_q, register_3_q, register_4_q, register_5_q, register_6_q,
       register_7_q, register_8_q, register_9_q, register_10_q, register_11_q, register_12_q, register_13_q,
       register_14_q, register_15_q, register_16_q, register_17_q, register_18_q, register_19_q,
       register_20_q, register_21_q, register_22_q, register_23_q, register_24_q, register_25_q,
       register_26_q, register_27_q, register_28_q, register_29_q, register_30_q, register_31_q,
       register_32_q;

  Demultiplexer #(.enable("false"), .select(5)) demultiplexer_1 (
    .out0(demultiplexer_1_out0), .out1(demultiplexer_1_out1), .out2(demultiplexer_1_out2),
    .out3(demultiplexer_1_out3), .out4(demultiplexer_1_out4), .out5(demultiplexer_1_out5),
    .out6(demultiplexer_1_out6), .out7(demultiplexer_1_out7), .out8(demultiplexer_1_out8),
    .out9(demultiplexer_1_out9), .out10(demultiplexer_1_out10), .out11(demultiplexer_1_out11),
    .out12(demultiplexer_1_out12), .out13(demultiplexer_1_out13), .out14(demultiplexer_1_out14),
    .out15(demultiplexer_1_out15), .out16(demultiplexer_1_out16), .out17(demultiplexer_1_out17),
    .out18(demultiplexer_1_out18), .out19(demultiplexer_1_out19), .out20(demultiplexer_1_out20),
    .out21(demultiplexer_1_out21), .out22(demultiplexer_1_out22), .out23(demultiplexer_1_out23),
    .out24(demultiplexer_1_out24), .out25(demultiplexer_1_out25), .out26(demultiplexer_1_out26),
    .out27(demultiplexer_1_out27), .out28(demultiplexer_1_out28), .out29(demultiplexer_1_out29),
    .out30(demultiplexer_1_out30), .out31(demultiplexer_1_out31), .in(Write), .sel(WReg));
  Register #(.width(32)) register_1 (
    .D(WData), .en(demultiplexer_1_out0), .clk(Clock_in), .Q(register_1_q), .clr(Write));
  Register #(.width(32)) register_2 (
    .D(WData), .en(demultiplexer_1_out1), .clk(Clock_in), .Q(register_2_q));  // open: clr
  Register #(.width(32)) register_3 (
    .D(WData), .en(demultiplexer_1_out2), .clk(Clock_in), .Q(register_3_q), .clr(undriven));
  Register #(.width(32)) register_4 (
    .D(WData), .en(demultiplexer_1_out3), .clk(Clock_in), .Q(register_4_q));  // open: clr
  Register #(.width(32)) register_5 (
    .D(WData), .en(demultiplexer_1_out4), .clk(Clock_in), .Q(register_5_q), .clr(undriven_2));
  Register #(.width(32)) register_6 (
    .D(WData), .en(demultiplexer_1_out5), .clk(Clock_in), .Q(register_6_q));  // open: clr
  Register #(.width(32)) register_7 (
    .D(WData), .en(demultiplexer_1_out6), .clk(Clock_in), .Q(register_7_q), .clr(undriven_3));
  Register #(.width(32)) register_8 (
    .D(WData), .en(demultiplexer_1_out7), .clk(Clock_in), .Q(register_8_q));  // open: clr
  Register #(.width(32)) register_9 (
    .D(WData), .en(demultiplexer_1_out8), .clk(Clock_in), .Q(register_9_q), .clr(undriven_4));
  Register #(.width(32)) register_10 (
    .D(WData), .en(demultiplexer_1_out9), .clk(Clock_in), .Q(register_10_q));  // open: clr
  Register #(.width(32)) register_11 (
    .D(WData), .en(demultiplexer_1_out10), .clk(Clock_in), .Q(register_11_q), .clr(undriven_5));
  Register #(.width(32)) register_12 (
    .D(WData), .en(demultiplexer_1_out11), .clk(Clock_in), .Q(register_12_q));  // open: clr
  Register #(.width(32)) register_13 (
    .D(WData), .en(demultiplexer_1_out12), .clk(Clock_in), .Q(register_13_q), .clr(undriven_6));
  Register #(.width(32)) register_14 (
    .D(WData), .en(demultiplexer_1_out13), .clk(Clock_in), .Q(register_14_q));  // open: clr
  Register #(.width(32)) register_15 (
    .D(WData), .en(demultiplexer_1_out14), .clk(Clock_in), .Q(register_15_q), .clr(undriven_7));
  Register #(.width(32)) register_16 (
    .D(WData), .en(demultiplexer_1_out15), .clk(Clock_in), .Q(register_16_q));  // open: clr
  Register #(.width(32)) register_17 (
    .D(WData), .en(demultiplexer_1_out16), .clk(Clock_in), .Q(register_17_q), .clr(undriven_8));
  Register #(.width(32)) register_18 (
    .D(WData), .en(demultiplexer_1_out17), .clk(Clock_in), .Q(register_18_q));  // open: clr
  Register #(.width(32)) register_19 (
    .D(WData), .en(demultiplexer_1_out18), .clk(Clock_in), .Q(register_19_q), .clr(undriven_9));
  Register #(.width(32)) register_20 (
    .D(WData), .en(demultiplexer_1_out19), .clk(Clock_in), .Q(register_20_q));  // open: clr
  Register #(.width(32)) register_21 (
    .D(WData), .en(demultiplexer_1_out20), .clk(Clock_in), .Q(register_21_q), .clr(undriven_10));
  Register #(.width(32)) register_22 (
    .D(WData), .en(demultiplexer_1_out21), .clk(Clock_in), .Q(register_22_q));  // open: clr
  Register #(.width(32)) register_23 (
    .D(WData), .en(demultiplexer_1_out22), .clk(Clock_in), .Q(register_23_q), .clr(undriven_11));
  Register #(.width(32)) register_24 (
    .D(WData), .en(demultiplexer_1_out23), .clk(Clock_in), .Q(register_24_q));  // open: clr
  Register #(.width(32)) register_25 (
    .D(WData), .en(demultiplexer_1_out24), .clk(Clock_in), .Q(register_25_q), .clr(undriven_12));
  Register #(.width(32)) register_26 (
    .D(WData), .en(demultiplexer_1_out25), .clk(Clock_in), .Q(register_26_q));  // open: clr
  Register #(.width(32)) register_27 (
    .D(WData), .en(demultiplexer_1_out26), .clk(Clock_in), .Q(register_27_q), .clr(undriven_13));
  Register #(.width(32)) register_28 (
    .D(WData), .en(demultiplexer_1_out27), .clk(Clock_in), .Q(register_28_q));  // open: clr
  Register #(.width(32)) register_29 (
    .D(WData), .en(demultiplexer_1_out28), .clk(Clock_in), .Q(register_29_q), .clr(undriven_14));
  Register #(.width(32)) register_30 (
    .D(WData), .en(demultiplexer_1_out29), .clk(Clock_in), .Q(register_30_q));  // open: clr
  Register #(.width(32)) register_31 (
    .D(WData), .en(demultiplexer_1_out30), .clk(Clock_in), .Q(register_31_q), .clr(undriven_15));
  Register #(.width(32)) register_32 (
    .D(WData), .en(demultiplexer_1_out31), .clk(Clock_in), .Q(register_32_q));  // open: clr
  Multiplexer #(.enable("false"), .select(5), .width(32)) multiplexer_1 (
    .in0(register_1_q), .in1(register_2_q), .in2(register_3_q), .in3(register_4_q), .in4(register_5_q),
    .in5(register_6_q), .in6(register_7_q), .in7(register_8_q), .in8(register_9_q), .in9(register_10_q),
    .in10(register_11_q), .in11(register_12_q), .in12(register_13_q), .in13(register_14_q),
    .in14(register_15_q), .in15(register_16_q), .in16(register_17_q), .in17(register_18_q),
    .in18(register_19_q), .in19(register_20_q), .in20(register_21_q), .in21(register_22_q),
    .in22(register_23_q), .in23(register_24_q), .in24(register_25_q), .in25(register_26_q),
    .in26(register_27_q), .in27(register_28_q), .in28(register_29_q), .in29(register_30_q),
    .in30(register_31_q), .in31(register_32_q), .out(RData1), .sel(RReg1));
  Multiplexer #(.enable("false"), .select(5), .width(32)) multiplexer_2 (
    .in0(register_1_q), .in1(register_2_q), .in2(register_3_q), .in3(register_4_q), .in4(register_5_q),
    .in5(register_6_q), .in6(register_7_q), .in7(register_8_q), .in8(register_9_q), .in9(register_10_q),
    .in10(register_11_q), .in11(register_12_q), .in12(register_13_q), .in13(register_14_q),
    .in14(register_15_q), .in15(register_16_q), .in16(register_17_q), .in17(register_18_q),
    .in18(register_19_q), .in19(register_20_q), .in20(register_21_q), .in21(register_22_q),
    .in22(register_23_q), .in23(register_24_q), .in24(register_25_q), .in25(register_26_q),
    .in26(register_27_q), .in27(register_28_q), .in28(register_29_q), .in29(register_30_q),
    .in30(register_31_q), .in31(register_32_q), .out(RData2), .sel(RReg2));
endmodule

module ImmGen (
  input  [31:0] Instructions,
  output [31:0] IMM32
);

  Multiplexer #(.enable("false"), .select(2)) multiplexer_1 (
    .in0(Instructions[20]), .in1(Instructions[7]), .in3(1'b0), .out(IMM32[0]), .sel(Instructions[6:5]));  // open: in2
  Multiplexer #(.enable("false"), .width(4)) multiplexer_2 (
    .in0(Instructions[24:21]), .in1(Instructions[11:8]), .out(IMM32[4:1]), .sel(Instructions[5]));
  Multiplexer #(.enable("false")) multiplexer_3 (
    .in0(Instructions[31]), .in1(Instructions[7]), .out(IMM32[11]), .sel(Instructions[6]));
  assign IMM32[31:12] = {{19{Instructions[31]}}, Instructions[31]};  // Bit_Extender bit_extender_1

  assign IMM32[10:5] = Instructions[30:25];
endmodule

module Control (
  input  I6,
  input  I5,
  input  I4,
  input  I3,
  input  I2,
  input  I1,
  input  I0,
  output MemtoReg,
  output RegWrite,
  output MemRead,
  output MemWrite,
  output Branch
);

  wire not_1_out, not_2_out;

  not not_1 (not_1_out, I6);
  not not_2 (not_2_out, I5);
  not not_3 (MemtoReg, I4);
  or or_1 (RegWrite, not_2_out, I4);
  and and_1 (MemRead, not_2_out, MemtoReg);
  and and_2 (MemWrite, not_1_out, I5, MemtoReg);

  assign Branch = I6;
endmodule

module InstructionMemory (
  input  [23:0] Address,
  input  Clock_in,
  output [31:0] Instructions
);

  wire not_1_out;
  wire [31:0] undriven;

  RAM #(.addrWidth(22), .asyncread("true"), .dataWidth(32)) ram_1 (
    .addr(Address[23:2]), .we(1'b0), .oe(not_1_out), .din(undriven), .dout(Instructions));  // open: clk
  not not_1 (not_1_out, Clock_in);
endmodule

module DataMemory (
  input  [25:0] Address,
  input  MemWrite,
  input  MemRead,
  input  Clock_In,
  input  [31:0] WriteData,
  output [31:0] ReadData
);

  RAM #(.addrWidth(24), .asyncread("true"), .dataWidth(32)) ram_1 (
    .addr(Address[25:2]), .we(MemWrite), .oe(MemRead), .clk(Clock_In), .din(WriteData), .dout(ReadData));
endmodule
